# Fritzing sketch GOOGLE_Assistant (saved by Fritzing 0.9.3b)

parts:
  U1 = NodeMCU V3.0
  HLK-PM1 = HLK-PM01
  U2 = 2-Channel 5v Relay Shield [package=relay-2ch5v10a]
  LED1 = LEDs [package=led10mm]
  LED2 = LEDs [package=led10mm]
  U3 = SWITCH-SPST-2 [package=switch-spst-vertical]
  U4 = SWITCH-SPST-2 [package=switch-spst-vertical]

nets:
  N1: U1.D0, U2.IN1
  N2: U1.D1, U2.IN2
  N3: U1.D2, U3.P
  N4: U1.D3, U4.P
  N5: U1.GND, HLK-PM1.-Vo, U3.O
  VIN: U1.Vin, HLK-PM1.+Vo, U2.VCC
  N6: HLK-PM1.AC#0, U2.K1-In, U2.K2-In
  N7: HLK-PM1.AC#1, LED1.A, LED2.A
  N8: U2.K1-On, LED1.C
  N9: U2.K2-On, LED2.C

notes:
  Entrada 220v
  Lampara 1
  Lampara 2
  Salida 5v
  Teclas de pared

custom parts:
  NodeMCU V3.0: NodeMcu V3 Lua WIFI Development Board
  2-Channel 5v Relay Shield: 2 Channel 5v Relay Shield w. 2x SPD-06VDC-SD-C
  LEDs: LEDs Standard schematic elements and footprints for 5mm, 3mm, 1206, and 0603 sized LEDs. 5mm - Spark Fun Electronics SKU : COM-00529 (and others)

// code stored in the sketch: google.ino
#include <ESP8266WiFi.h>
#include "Adafruit_MQTT.h"
#include "Adafruit_MQTT_Client.h"

#define WIFI_SSID  "SyH"
#define WIFI_PASS "a1a2a3a4a5a6"

#define MQTT_SERV "io.adafruit.com"
#define MQTT_PORT 1883
#define MQTT_NAME "hrico"
#define MQTT_PASS "08c744131d6543b6826ddb941e5197b5"

#define relay D0 
#define relay1 D1 

//Set up MQTT and WiFi clients
WiFiClient client;
Adafruit_MQTT_Client mqtt(&client, MQTT_SERV, MQTT_PORT, MQTT_NAME, MQTT_PASS);

//Set up the feed you're subscribing to
Adafruit_MQTT_Subscribe onoff = Adafruit_MQTT_Subscribe(&mqtt, MQTT_NAME "/f/onoff");
Adafruit_MQTT_Subscribe onoff1 = Adafruit_MQTT_Subscribe(&mqtt, MQTT_NAME "/f/onoff1");

/***************************************************************/

void setup()
{
  Serial.begin(9600);

  //Connect to WiFi
  Serial.print("\n\nConnecting Wifi... ");
  WiFi.begin(WIFI_SSID, WIFI_PASS);
  while (WiFi.status() != WL_CONNECTED)
  {
    delay(500);
  }

  Serial.println("OK!");

  //Subscribe to the onoff feed
  mqtt.subscribe(&onoff);
  mqtt.subscribe(&onoff1);

  pinMode(relay, OUTPUT);
  pinMode(relay1, OUTPUT);
  digitalWrite(relay,HIGH);
  digitalWrite(relay1,HIGH);
}

/***************************************************************/

void loop()
{
  MQTT_connect();
  
  //Read from our subscription queue until we run out, or
  //wait up to 4 seconds for subscription to update
  Adafruit_MQTT_Subscribe * subscription;
  while ((subscription = mqtt.readSubscription(4000)))
  {
    //If we're in here, a subscription updated...
    if (subscription == &onoff)
    {
      //Print the new value to the serial monitor
      Serial.print("onoff: ");
      Serial.println((char*) onoff.lastread);
      
      //If the new value is  "ON", turn the light on.
      //Otherwise, turn it off.
      if (!strcmp((char*) onoff.lastread, "ON"))
      {
        //Active low logic
          digitalWrite(relay,LOW);
      }
      else
      {
          digitalWrite(relay,HIGH);
      }
    }
    if (subscription == &onoff1)
    {
      //Print the new value to the serial monitor
      Serial.print("onoff1: ");
      Serial.println((char*) onoff1.lastread);
      
      //If the new value is  "ON", turn the light on.
      //Otherwise, turn it off.
      if (!strcmp((char*) onoff1.lastread, "ON"))
      {
        //Active low logic
          digitalWrite(relay1,LOW);
      }
      else
      {
          digitalWrite(relay1,HIGH);
      }
    }
  
  }


  // ping the server to keep the mqtt connection alive
  if (!mqtt.ping())
  {
    mqtt.disconnect();
  }
}
/***************************************************************/

void MQTT_connect() 
{
  int8_t ret;

  // Stop if already connected.
  if (mqtt.connected()) 
  {
    return;
  }

  Serial.print("Connecting to MQTT... ");

  uint8_t retries = 3;
  while ((ret = mqtt.connect()) != 0) // connect will return 0 for connected
  { 
       Serial.println(mqtt.connectErrorString(ret));
       Serial.println("Retrying MQTT connection in 5 seconds...");
       mqtt.disconnect();
       delay(4000);  // wait 4 seconds
       retries--;
       if (retries == 0) 
       {
         // basically die and wait for WDT to reset me
         while (1);
       }
  }
  Serial.println("MQTT Connected!");
}
